# Fritzing sketch OSV (saved by Fritzing 0.9.3b)
breadboards: 1

parts:
  Part1 = Arduino Uno (Rev3)
  M5 = DC Motor
  U2 = LIPO-2000mAh [package=lipo-2000]
  M6 = DC Motor
  Q1 = Basic FET P-Channel [package="D2Pak [SMD]"]
  Q2 = Basic FET P-Channel [package="D2Pak [SMD]"]
  Q3 = Basic FET P-Channel [package="D2Pak [SMD]"]
  Q4 = Basic FET P-Channel [package="D2Pak [SMD]"]
  Q5 = Basic FET P-Channel [package="D2Pak [SMD]"]
  Q6 = Basic FET P-Channel [package="D2Pak [SMD]"]
  Q7 = Basic FET P-Channel [package="D2Pak [SMD]"]
  Q8 = Basic FET P-Channel [package="D2Pak [SMD]"]
  U3 = LIPO-2000mAh [package=lipo-2000]
  S1 = KY-026
  J1 = Basic Servo
  Part2 = Arduino Uno (Rev3)
  M7 = DC Motor
  M8 = DC Motor
  Q9 = Basic FET P-Channel [package="D2Pak [SMD]"]
  Q10 = Basic FET P-Channel [package="D2Pak [SMD]"]
  Q11 = Basic FET P-Channel [package="D2Pak [SMD]"]
  Q12 = Basic FET P-Channel [package="D2Pak [SMD]"]
  Q13 = Basic FET P-Channel [package="D2Pak [SMD]"]
  Q14 = Basic FET P-Channel [package="D2Pak [SMD]"]
  Q15 = Basic FET P-Channel [package="D2Pak [SMD]"]
  Q16 = Basic FET P-Channel [package="D2Pak [SMD]"]
  S2 = KY-026
  S3 = KY-026
  S4 = KY-026
  hc-sr1 = hc-sr04
  hc-sr2 = hc-sr04
  hc-sr3 = hc-sr04
  hc-sr4 = hc-sr04
  APC1 = APC220
  U4 = LIPO-2000mAh [package=lipo-2000]

nets:
  N1: Part1.D8, Q13.Gate, Q16.Gate
  N2: Part1.D9_PWM, Q1.Gate, Q4.Gate
  N3: Part1.D10_PWM/SS, Q5.Gate, Q8.Gate
  N4: Part1.D11_PWM/MOSI, J1.pulse
  N5: Part1.D0/RX, Part2.D0/RX
  N6: Part1.D1/TX, Part2.D1/TX
  N7: Part1.D2, Q9.Gate, Q12.Gate
  N8: Part1.D3_PWM, Q10.Gate, Q11.Gate
  N9: Part1.D5_PWM, Q2.Gate, Q3.Gate
  N10: Part1.D6_PWM, Q6.Gate, Q7.Gate
  N11: Part1.D7, Q14.Gate, Q15.Gate
  5V: Part1.5V, J1.vcc
  GND: Part1.GND, J1.gnd, U4.-
  N12: Part1.VIN, U4.+
  N13: M5.pin_1, Q5.source, Q6.drain
  N14: M5.pin_2, Q7.source, Q8.drain
  N15: U2.+, Q1.drain, Q3.drain, Q5.drain, Q7.drain, Q9.drain, Q11.drain, Q13.drain, Q15.drain
  N16: U2.-, Q2.source, Q4.source, Q6.source, Q8.source, Q10.source, Q12.source, Q14.source, Q16.source
  N17: M6.pin_1, Q1.source, Q2.drain
  N18: M6.pin_2, Q3.source, Q4.drain
  N19: U3.+, Part2.VIN
  GND_2: U3.-, S1.pin2, Part2.GND, S2.pin2, S3.pin2, S4.pin2, hc-sr2.GND, hc-sr3.GND, APC1.GND
  VCC: S1.pin3, Part2.5V, S2.pin3, S3.pin3, S4.pin3, hc-sr1.VCC, hc-sr2.VCC, hc-sr3.VCC, hc-sr4.VCC, APC1.VCC, APC1.EN, APC1.SET
  N20: S1.pin4, Part2.D3_PWM
  N21: Part2.A0, Part2.D7, hc-sr4.Trig
  N22: Part2.A1, Part2.D8, hc-sr1.Trig
  N23: Part2.A2, Part2.D9_PWM, hc-sr2.Trig
  N24: Part2.A3, Part2.D10_PWM/SS, hc-sr3.Trig
  N25: Part2.D11_PWM/MOSI, APC1.RXD
  N26: Part2.D12/MISO, APC1.TXD
  N27: Part2.D4, S3.pin4
  N28: Part2.D5_PWM, S2.pin4
  N29: Part2.D6_PWM, S4.pin4
  N30: M7.pin_1, Q9.source, Q10.drain
  N31: M7.pin_2, Q11.source, Q12.drain
  N32: M8.pin_1, Q13.source, Q14.drain
  N33: M8.pin_2, Q15.source, Q16.drain
  GND_3: hc-sr1.GND, hc-sr4.GND

custom parts:
  KY-026: ky-026 flame sensor module
  APC220: APC Series Transparent Transceiver Module
